// Logisim project projetoCirc.circ as structural Verilog: 22 circuits, main circuit [6] memoriaPalpite
module visual (
  input  in_1,
  input  in_2,
  input  Palpite_do,
  input  in_4,
  input  in_5,
  input  in_6,
  input  in_7,
  input  Palpite_do_2,
  input  in_9,
  input  in_10,
  output out_11
);

  wire _5_clockx, _5_clockx_2, _15_fimdejogo, _18_2_out_3, _18_3_out_3, _18_4_out_3, _18_5_out_3, _18_out_3,
       ACERTOU, and_1_out, and_3_out, and_4_out, and_6_out, and_7_out, and_8_out, and_10_out, and_11_out,
       and_12_out, and_13_out, and_15_out, and_16_out, \Avançar_estado , Chutando_X, Chutando_Y, Clock,
       Configure, Confirmar_palpite, ContadorNormal, demultiplexer_1_out0, demultiplexer_1_out1, Empate,
       end0, end1, Fim_de_jogo, gdM, gdS, guM, guS, igual, Jogador_da_vez__placar, maior, menor, not_1_out,
       nP0, nP1, nX, nY, or_1_out, or_2_out, P0_venceu, P1_venceu, Reset, Resultado, slumb, zerar0, zerar1,
       zerou0, zerou1;
  wire [3:0] _6_2_out_4, _6_out_4, Chute_de_X, Chute_de_Y, dM, dM1, dS, dS1, multiplexer_1_out, placar0,
       placar1, rD0, rD1, rU0, rU1, uM, uM1, uS, uS1, Visor_de_P0, Visor_de_P1;

  Hex_Digit_Display hex_digit_display_1 (.value(rD0));  // open: dp
  Hex_Digit_Display hex_digit_display_2 (.value(dM));  // open: dp
  Hex_Digit_Display hex_digit_display_3 (.value(rU0));  // open: dp
  LED led_1 ();  // open: in
  LED led_2 ();  // open: in
  Hex_Digit_Display hex_digit_display_4 (.value(dS));  // open: dp
  Hex_Digit_Display hex_digit_display_5 (.value(uM));  // open: dp
  _7_Segment_Display u_7_segment_display_1 (.g(nP0));  // open: f, a, b, e, d, c, dp
  Hex_Digit_Display hex_digit_display_6 (.value(Visor_de_P0));  // open: dp
  LED led_3 (.in(P0_venceu));
  Hex_Digit_Display hex_digit_display_7 (.value(uS));  // open: dp
  LED led_4 (.in(Fim_de_jogo));
  LED led_5 (.in(Empate));
  LED led_6 (.in(P1_venceu));
  LED led_7 (.in(Chutando_X));
  _7_Segment_Display u_7_segment_display_2 (.g(nX));  // open: f, a, b, e, d, c, dp
  LED led_8 (.in(maior));
  Hex_Digit_Display hex_digit_display_8 (.value(rD1));  // open: dp
  LED led_9 (.in(Chutando_Y));
  Button button_1 (.out(Confirmar_palpite));
  Hex_Digit_Display hex_digit_display_9 (.value(Chute_de_X));  // open: dp
  LED led_10 (.in(igual));
  Hex_Digit_Display hex_digit_display_10 (.value(rU1));  // open: dp
  LED led_11 (.in(Resultado));
  Button button_2 (.out(\Avançar_estado ));
  _7_Segment_Display u_7_segment_display_3 (.g(nY));  // open: f, a, b, e, d, c, dp
  Hex_Digit_Display hex_digit_display_11 (.value(Chute_de_Y));  // open: dp
  LED led_12 (.in(menor));
  LED led_13 (.in(ACERTOU));
  Button u_dM (.out(gdM));
  Hex_Digit_Display hex_digit_display_12 (.value(dM1));  // open: dp
  Button u_uM (.out(guM));
  LED led_14 ();  // open: in
  LED led_15 ();  // open: in
  Hex_Digit_Display hex_digit_display_13 (.value(uM1));  // open: dp
  _7_Segment_Display u_7_segment_display_4 (.g(nP1));  // open: f, a, b, e, d, c, dp
  Button button_3 (.out(Reset));
  Button u_dS (.out(gdS));
  Button u_uS (.out(guS));
  Hex_Digit_Display hex_digit_display_14 (.value(dS1));  // open: dp
  Hex_Digit_Display hex_digit_display_15 (.value(uS1));  // open: dp
  Hex_Digit_Display hex_digit_display_16 (.value(Visor_de_P1));  // open: dp
  and and_1 (and_1_out, slumb, end1);
  _8__visualizadorPalpites _8 (.e3({in_7, Palpite_do_2, in_9, in_10}), .n(nP0), .out_3(Visor_de_P0));
  and and_2 (zerou1, slumb, end1);
  and and_3 (and_3_out, slumb, end0);
  _18__logicaEstadoPermanente _18 (.in_1(and_3_out), .Reset(Reset), .out_3(_18_out_3));
  _18__logicaEstadoPermanente _18_2 (.in_1(and_1_out), .Reset(Reset), .out_3(_18_2_out_3));
  and and_4 (and_4_out, _18_2_out_3, ContadorNormal);
  and and_5 (zerou0, slumb, end0);
  _8__visualizadorPalpites _8_2 (.e3({Palpite_do, in_4, in_5, in_6}), .n(nP1), .out_3(Visor_de_P1));
  _18__logicaEstadoPermanente _18_3 (.in_1(zerou1), .Reset(Reset), .out_3(_18_3_out_3));
  and and_6 (and_6_out, _18_out_3, ContadorNormal);
  Demultiplexer demultiplexer_1 (
    .out0(demultiplexer_1_out0), .out1(demultiplexer_1_out1), .in(ContadorNormal), .sel(out_11));  // open: en
  or or_1 (or_1_out, demultiplexer_1_out1, and_4_out);
  _18__logicaEstadoPermanente _18_4 (.in_1(zerou0), .Reset(Reset), .out_3(_18_4_out_3));
  _18__logicaEstadoPermanente u_18_logicaestadopermanente_1 (.in_1(in_1), .Reset(Reset), .out_3(slumb));
  Multiplexer #(.width(4)) multiplexer_1 (
    .in0({in_7, Palpite_do_2, in_9, in_10}), .in1({Palpite_do, in_4, in_5, in_6}), .out(multiplexer_1_out),
    .sel(out_11));  // open: en
  _17__mudaJogador _17 (.Resultado(Resultado), .Z1(zerou1), .Z0(zerou0), .out_4(out_11));
  and and_7 (and_7_out, ~_18_3_out_3, or_2_out);  // AND_Gate
  or or_2 (or_2_out, and_6_out, demultiplexer_1_out0);
  and and_8 (and_8_out, or_1_out, ~_18_4_out_3);  // AND_Gate
  and and_9 (Configure, in_2, ~slumb);  // AND_Gate
  _5__LEDS _5 (
    .Chutar(Confirmar_palpite), .in_2(\Avançar_estado ), .x(Chutando_X), .y(Chutando_Y), .c(Resultado),
    .clockX(_5_clockx), .clockX_2(_5_clockx_2));
  _6__memoriaPalpite _6 (.in_1(_5_clockx), .in_2(multiplexer_1_out), .reset(Reset), .out_4(_6_out_4));
  _6__memoriaPalpite _6_2 (.in_1(_5_clockx_2), .in_2(multiplexer_1_out), .reset(Reset), .out_4(_6_2_out_4));
  _12__relogioOrganizado _12 (
    .Clock(and_7_out), .Config(Configure), .Reset(Reset), .out_8(dM), .out_9(uM), .out_10(dS), .out_11(uS),
    .dM(gdM), .uM(guM), .dS(gdS), .uS(guS), .Fim(end1));
  _12__relogioOrganizado u_12_relogioorganizado_1 (
    .Clock(and_8_out), .Config(Configure), .Reset(Reset), .out_8(dM1), .out_9(uM1), .out_10(dS1),
    .out_11(uS1), .dM(gdM), .uM(guM), .dS(gdS), .uS(guS), .Fim(end0));
  _8__visualizadorPalpites _8_3 (.e3(_6_out_4), .n(nX), .out_3(Chute_de_X));
  _8__visualizadorPalpites _8_4 (.e3(_6_2_out_4), .n(nY), .out_3(Chute_de_Y));
  Clock clock_1 (.out(Clock));
  _17__mudaJogador _17_2 (.Resultado(Chutando_X), .out_4(Jogador_da_vez__placar));  // open: Z1, Z0
  not not_1 (not_1_out, Jogador_da_vez__placar);
  _18__logicaEstadoPermanente _18_5 (.in_1(in_1), .Reset(Reset), .out_3(_18_5_out_3));
  _7__somador _7 (
    .palpite_Coord__x(Chute_de_X), .palpite_Coord__Y(Chute_de_Y), .in_1(Resultado), .in_4(and_10_out),
    .maior(maior), .igual__soma(igual), .menor(menor), .igual__coordenadas(ACERTOU));
  and and_10 (and_10_out, Chutando_X, ACERTOU);
  and and_11 (and_11_out, ACERTOU, Jogador_da_vez__placar);
  and and_12 (and_12_out, ACERTOU, not_1_out);
  _15__placarFinal _15 (
    .placar0(placar0), .placar1(placar1), .tempo0(end0), .tempo1(end1), .FimdeJogo(_15_fimdejogo),
    .venceu0(P0_venceu), .empate(Empate), .venceu1(P1_venceu));
  and and_13 (and_13_out, slumb, _15_fimdejogo);
  and and_14 (ContadorNormal, Clock, ~Fim_de_jogo, _18_5_out_3);  // AND_Gate
  and and_15 (and_15_out, in_1, end1);
  _18__logicaEstadoPermanente _18_6 (.in_1(and_15_out), .out_3(zerar1));  // open: Reset
  _1__Pontuador _1 (.in_1(and_11_out), .Reset(Reset), .out_3(placar1));
  _1__Pontuador _1_2 (.in_1(and_12_out), .Reset(Reset), .out_3(placar0));
  _18__logicaEstadoPermanente _18_7 (.in_1(and_13_out), .Reset(Reset), .out_3(Fim_de_jogo));
  and and_16 (and_16_out, in_1, end0);
  _18__logicaEstadoPermanente _18_8 (.in_1(and_16_out), .out_3(zerar0));  // open: Reset
  _16__mostraEmDecimal _16 (.e3(placar1[3]), .e2(placar1[2]), .e1(placar1[1]), .e0(placar1[0]), .d(rD1), .u(rU1));
  _16__mostraEmDecimal _16_2 (.e3(placar0[3]), .e2(placar0[2]), .e1(placar0[1]), .e0(placar0[0]), .d(rD0), .u(rU0));

  // Other names for the same wires on the sheet: y0 = in_10; y1 = in_9; y2 = Palpite_do_2; y3 = in_7; x0 = in_6;
  //   x1 = in_5; x2 = in_4; x3 = Palpite_do; Configurando = in_2; Jogador_da_vez = out_11; Start = in_1

  // Notes on the sheet:
  //   Placar do P0
  //   Player 0
  //   RESULTADO
  //   Guess the Number
  //   ESTADO ATUAL
  //   SEU PALPITE É
  //   SUA SOMA FOI
  //   XTREME
  //   Placar do P1
  //   PAINEL DE CONTROLE
  //   Player 1
endmodule

module MAIN__Guess_The_Number (
  input  Palpite_do,
  input  in_2,
  input  in_3,
  input  in_4,
  input  in_5,
  input  Palpite_do_2,
  input  in_7,
  input  in_8
);

  wire _5_clockx, _5_clockx_2, ACERTOU, and_1_out, and_2_out, and_4_out, and_5_out, and_6_out, and_7_out,
       \Avançar_estado , Chutando_X, Chutando_Y, clock_1_out, Configurando, Confirmar_palpite, Empate, end0,
       end1, Fim_de_jogo, gdM, gdS, guM, guS, igual, maior, menor, not_1_out, nP0, nP1, nX, nY, P0_venceu,
       P1_venceu, player, Reset, Resultado, Start, startt_1_p2, startt_1_p3, startt_1_p4, undriven,
       undriven_2;
  wire [3:0] _6_2_out_4, _6_out_4, Chute_de_X, Chute_de_Y, dM, dM1, dS, dS1, multiplexer_1_out, placar0,
       placar1, rD0, rD1, rU0, rU1, uM, uM1, uS, uS1, Visor_de_P0, Visor_de_P1;

  Hex_Digit_Display hex_digit_display_1 (.value(rD0));  // open: dp
  Hex_Digit_Display hex_digit_display_2 (.value(dM));  // open: dp
  Hex_Digit_Display hex_digit_display_3 (.value(rU0));  // open: dp
  LED led_1 ();  // open: in
  LED led_2 ();  // open: in
  Hex_Digit_Display hex_digit_display_4 (.value(uM));  // open: dp
  Hex_Digit_Display hex_digit_display_5 (.value(dS));  // open: dp
  _7_Segment_Display u_7_segment_display_1 (.g(nP0));  // open: f, a, b, e, d, c, dp
  Hex_Digit_Display hex_digit_display_6 (.value(Visor_de_P0));  // open: dp
  LED led_3 (.in(Fim_de_jogo));
  LED led_4 (.in(P0_venceu));
  Hex_Digit_Display hex_digit_display_7 (.value(uS));  // open: dp
  LED led_5 (.in(Empate));
  LED led_6 (.in(P1_venceu));
  LED led_7 (.in(Chutando_X));
  _7_Segment_Display u_7_segment_display_2 (.g(nX));  // open: f, a, b, e, d, c, dp
  LED led_8 (.in(maior));
  Hex_Digit_Display hex_digit_display_8 (.value(rD1));  // open: dp
  LED led_9 (.in(Chutando_Y));
  Button button_1 (.out(Confirmar_palpite));
  Hex_Digit_Display hex_digit_display_9 (.value(Chute_de_X));  // open: dp
  LED led_10 (.in(igual));
  Hex_Digit_Display hex_digit_display_10 (.value(rU1));  // open: dp
  LED led_11 (.in(Resultado));
  Button button_2 (.out(\Avançar_estado ));
  _7_Segment_Display u_7_segment_display_3 (.g(nY));  // open: f, a, b, e, d, c, dp
  Hex_Digit_Display hex_digit_display_11 (.value(Chute_de_Y));  // open: dp
  LED led_12 (.in(ACERTOU));
  LED led_13 (.in(menor));
  Button button_3 (.out(Start));
  Button u_dM (.out(gdM));
  Hex_Digit_Display hex_digit_display_12 (.value(dM1));  // open: dp
  Button button_4 ();  // open: out
  Button u_uM (.out(guM));
  LED led_14 ();  // open: in
  LED led_15 ();  // open: in
  Hex_Digit_Display hex_digit_display_13 (.value(uM1));  // open: dp
  _7_Segment_Display u_7_segment_display_4 (.g(nP1));  // open: f, a, b, e, d, c, dp
  Button button_5 (.out(Reset));
  LED led_16 (.in(Configurando));
  Button u_dS (.out(gdS));
  Button u_uS (.out(guS));
  Hex_Digit_Display hex_digit_display_14 (.value(uS1));  // open: dp
  Hex_Digit_Display hex_digit_display_15 (.value(dS1));  // open: dp
  Hex_Digit_Display hex_digit_display_16 (.value(Visor_de_P1));  // open: dp
  Clock clock_1 (.out(clock_1_out));
  _16__mostraEmDecimal u_16_mostraemdecimal_1 (.e3(in_8), .e2(in_7), .e1(Palpite_do_2), .e0(in_5));  // open: d, u
  _16__mostraEmDecimal u_16_mostraemdecimal_2 (.e3(in_4), .e2(in_3), .e1(in_2), .e0(Palpite_do));  // open: d, u
  and and_1 (and_1_out, clock_1_out, ~end1, player);  // AND_Gate
  and and_2 (and_2_out, clock_1_out, ~end0, ~player);  // AND_Gate
  // startt startt_1: pin names not known; wires that end beside it: and_1_out, startt_1_p2, startt_1_p3, startt_1_p4
  // AND_Gate and_3 has open pins: in0=startt_1_p3, in1=Configurando, out=open
  Multiplexer #(.width(4)) multiplexer_1 (
    .in0({Palpite_do, in_2, in_3, in_4}), .in1({in_5, Palpite_do_2, in_7, in_8}), .out(multiplexer_1_out),
    .sel(player));  // open: en
  _12__relogioOrganizado u_12_relogioorganizado_1 (
    .Clock(startt_1_p4), .Config(undriven), .Reset(Reset), .out_8(dM), .out_9(uM), .out_10(dS), .out_11(uS),
    .dM(gdM), .uM(guM), .dS(gdS), .uS(guS), .Fim(end1));
  _12__relogioOrganizado u_12_relogioorganizado_2 (
    .Clock(and_2_out), .Config(undriven_2), .Reset(Reset), .out_8(dM1), .out_9(uM1), .out_10(dS1),
    .out_11(uS1), .dM(gdM), .uM(guM), .dS(gdS), .uS(guS), .Fim(end0));
  _5__LEDS _5 (
    .Chutar(Confirmar_palpite), .in_2(\Avançar_estado ), .x(Chutando_X), .y(Chutando_Y), .c(Resultado),
    .clockX(_5_clockx), .clockX_2(_5_clockx_2));
  _6__memoriaPalpite _6 (.in_1(_5_clockx), .in_2(multiplexer_1_out), .reset(Reset), .out_4(_6_out_4));
  _6__memoriaPalpite _6_2 (.in_1(_5_clockx_2), .in_2(multiplexer_1_out), .reset(Reset), .out_4(_6_2_out_4));
  _8__visualizadorPalpites _8 (.e3(_6_out_4), .n(nX), .out_3(Chute_de_X));
  _8__visualizadorPalpites _8_2 (.e3(_6_2_out_4), .n(nY), .out_3(Chute_de_Y));
  and and_4 (and_4_out, Chutando_Y, \Avançar_estado );
  not not_1 (not_1_out, and_4_out);
  _7__somador _7 (
    .palpite_Coord__x(_6_out_4), .palpite_Coord__Y(_6_2_out_4), .in_1(Resultado), .in_4(and_5_out),
    .maior(maior), .igual__soma(igual), .menor(menor), .igual__coordenadas(ACERTOU));
  and and_5 (and_5_out, Chutando_X, ACERTOU);
  and and_6 (and_6_out, ACERTOU, and_4_out);
  and and_7 (and_7_out, ACERTOU, not_1_out);
  _15__placarFinal u_15_placarfinal_1 (
    .placar0(placar0), .placar1(placar1), .tempo0(end0), .tempo1(end1), .venceu0(P0_venceu), .empate(Empate),
    .venceu1(P1_venceu));  // open: FimdeJogo
  _1__Pontuador _1 (.in_1(and_6_out), .Reset(Reset), .out_3(placar1));
  _1__Pontuador _1_2 (.in_1(and_7_out), .Reset(Reset), .out_3(placar0));
  _16__mostraEmDecimal u_16_mostraemdecimal_3 (
    .e3(placar1[3]), .e2(placar1[2]), .e1(placar1[1]), .e0(placar1[0]), .d(rD1), .u(rU1));
  _16__mostraEmDecimal u_16_mostraemdecimal_4 (
    .e3(placar0[3]), .e2(placar0[2]), .e1(placar0[1]), .e0(placar0[0]), .d(rD0), .u(rU0));

  // Other names for the same wires on the sheet: y0 = in_8; y1 = in_7; y2 = Palpite_do_2; y3 = in_5; x0 = in_4;
  //   x1 = in_3; x2 = in_2; x3 = Palpite_do

  // Notes on the sheet:
  //   Placar do P0
  //   Player 0
  //   RESULTADO
  //   Guess the Number
  //   ESTADO ATUAL
  //   SEU PALPITE É
  //   SUA SOMA FOI
  //   XTREME
  //   Placar do P1
  //   PAINEL DE CONTROLE
  //   Player 1
  //   Palpite do
  //   jogador 0
  //   Palpite do
  //   jogador 1
endmodule

module _1__Pontuador (
  input  in_1,
  input  Reset,
  output [3:0] out_3
);

  wire n2_transicaopontuador_1_s0, n2_transicaopontuador_1_s1, n2_transicaopontuador_1_s2,
       n2_transicaopontuador_1_s3;

  D_Flip_Flop d_ff_1 (.clk(in_1), .D(n2_transicaopontuador_1_s3), .Q(out_3[3]), .reset(Reset));  // open: Qn, preset, en
  D_Flip_Flop d_ff_2 (.clk(in_1), .D(n2_transicaopontuador_1_s2), .Q(out_3[2]), .reset(Reset));  // open: Qn, preset, en
  D_Flip_Flop d_ff_3 (.clk(in_1), .D(n2_transicaopontuador_1_s1), .Q(out_3[1]), .reset(Reset));  // open: Qn, preset, en
  _2__transicaoPontuador u_2_transicaopontuador_1 (
    .e0(out_3[3]), .e1(out_3[2]), .e2(out_3[1]), .e3(out_3[0]), .x(1'b1), .s3(n2_transicaopontuador_1_s3),
    .s2(n2_transicaopontuador_1_s2), .s1(n2_transicaopontuador_1_s1), .s0(n2_transicaopontuador_1_s0));
  D_Flip_Flop d_ff_4 (.clk(in_1), .D(n2_transicaopontuador_1_s0), .Q(out_3[0]), .reset(Reset));  // open: Qn, preset, en
endmodule

// [2]
module _2__transicaoPontuador (
  input  e0,
  input  e1,
  input  e2,
  input  e3,
  input  x,
  output s3,
  output s2,
  output s1,
  output s0
);

  wire and_1_out, and_2_out, and_3_out, and_4_out, and_5_out, and_6_out, and_7_out, and_8_out, and_9_out,
       and_10_out, and_11_out, and_12_out, and_13_out, and_14_out, not_1_out, not_2_out, not_3_out,
       not_4_out, not_5_out, not_6_out, not_7_out, not_8_out, not_9_out, not_10_out, not_11_out, not_12_out,
       not_13_out, not_14_out;

  not not_1 (not_1_out, e0);
  not not_2 (not_2_out, e1);
  not not_3 (not_3_out, e2);
  not not_4 (not_4_out, e3);
  not not_5 (not_5_out, x);
  not not_6 (not_6_out, e1);
  not not_7 (not_7_out, e2);
  not not_8 (not_8_out, e3);
  not not_9 (not_9_out, x);
  not not_10 (not_10_out, e2);
  not not_11 (not_11_out, e3);
  not not_12 (not_12_out, x);
  not not_13 (not_13_out, e3);
  not not_14 (not_14_out, x);
  and and_1 (and_1_out, not_1_out, e1, e2, e3, x);
  and and_2 (and_2_out, e0, not_2_out);
  and and_3 (and_3_out, e0, not_3_out);
  and and_4 (and_4_out, e0, not_4_out);
  and and_5 (and_5_out, e0, not_5_out);
  and and_6 (and_6_out, not_6_out, e2, e3, x);
  and and_7 (and_7_out, e1, not_7_out);
  and and_8 (and_8_out, e1, not_8_out);
  and and_9 (and_9_out, e1, not_9_out);
  and and_10 (and_10_out, not_10_out, e3, x);
  and and_11 (and_11_out, e2, not_11_out);
  and and_12 (and_12_out, e2, not_12_out);
  and and_13 (and_13_out, not_13_out, x);
  and and_14 (and_14_out, e3, not_14_out);
  or or_1 (s3, and_1_out, and_2_out, and_3_out, and_4_out, and_5_out);
  or or_2 (s2, and_6_out, and_7_out, and_8_out, and_9_out);
  or or_3 (s1, and_10_out, and_11_out, and_12_out);
  or or_4 (s0, and_13_out, and_14_out);
endmodule

module _3__logicaLEDS (
  input  in_1,
  input  in_2,
  output out_3,
  output out_4,
  output out_5
);

  and and_1 (out_3, ~in_1, ~in_2);  // AND_Gate
  and and_2 (out_4, ~in_1, in_2);  // AND_Gate
  and and_3 (out_5, in_1, ~in_2);  // AND_Gate
endmodule

module _4__transicaoLEDS (
  input  e1,
  input  e0,
  output s1,
  output s0
);

  wire not_1_out, not_2_out;

  not not_1 (not_1_out, e1);
  not not_2 (not_2_out, e0);
  and and_1 (s0, not_1_out, not_2_out);

  assign s1 = e0;
endmodule

module _5__LEDS (
  input  Chutar,
  input  in_2,
  output x,
  output y,
  output c,
  output clockX,
  output clockX_2
);

  wire _4_s0, _4_s1, and_1_out, and_2_out, d_ff_1_q, d_ff_2_q, not_1_out, not_2_out, not_3_out, not_4_out,
       not_6_out, not_7_out;

  _3__logicaLEDS _3 (.in_1(d_ff_1_q), .in_2(d_ff_2_q), .out_3(x), .out_4(y), .out_5(c));
  D_Flip_Flop d_ff_1 (.clk(in_2), .D(_4_s1), .Q(d_ff_1_q));  // open: Qn, preset, en, reset
  _4__transicaoLEDS _4 (.e1(d_ff_1_q), .e0(d_ff_2_q), .s1(_4_s1), .s0(_4_s0));
  D_Flip_Flop d_ff_2 (.clk(in_2), .D(_4_s0), .Q(d_ff_2_q));  // open: Qn, preset, en, reset
  and and_1 (and_1_out, x, Chutar);
  and and_2 (and_2_out, Chutar, y);
  not not_1 (not_1_out, and_1_out);
  not not_2 (not_2_out, not_1_out);
  not not_3 (not_3_out, not_4_out);
  not not_4 (not_4_out, and_2_out);
  not not_5 (clockX, not_6_out);
  not not_6 (not_6_out, not_2_out);
  not not_7 (not_7_out, not_3_out);
  not not_8 (clockX_2, not_7_out);
endmodule

module _6__memoriaPalpite (
  input  in_1,
  input  [3:0] in_2,
  input  reset,
  output [3:0] out_4
);

  D_Flip_Flop d_ff_1 (.clk(in_1), .D(in_2[0]), .Q(out_4[0]), .reset(reset));  // open: Qn, preset, en
  D_Flip_Flop d_ff_2 (.clk(in_1), .D(in_2[1]), .Q(out_4[1]), .reset(reset));  // open: Qn, preset, en
  D_Flip_Flop d_ff_3 (.clk(in_1), .D(in_2[2]), .Q(out_4[2]), .reset(reset));  // open: Qn, preset, en
  D_Flip_Flop d_ff_4 (.clk(in_1), .D(in_2[3]), .Q(out_4[3]), .reset(reset));  // open: Qn, preset, en
endmodule

module _7__somador (
  input  in_1,
  input  [3:0] palpite_Coord__x,
  input  [3:0] palpite_Coord__Y,
  input  in_4,
  output maior,
  output igual__soma,
  output menor,
  output igual__coordenadas
);

  wire and_1_out, comparator_1_eq, comparator_2_eq, comparator_3_eq, comparator_3_gt, comparator_3_lt;
  wire [3:0] Coord__X_out, Coord__Y_out;
  wire [4:0] adder_1_out, adder_2_out, bit_extender_1_out, bit_extender_2_out, bit_extender_3_out,
       bit_extender_4_out;

  Random #(.width(4), .seed(4)) Coord__X (.clk(in_4), .out(Coord__X_out));  // open: next, clr
  Random #(.width(4)) Coord__Y (.clk(in_4), .out(Coord__Y_out));  // open: next, clr
  assign bit_extender_1_out = {{1{palpite_Coord__x[3]}}, palpite_Coord__x};  // Bit_Extender bit_extender_1
  assign bit_extender_2_out = {{1{palpite_Coord__Y[3]}}, palpite_Coord__Y};  // Bit_Extender bit_extender_2
  assign bit_extender_3_out = {{1{Coord__X_out[3]}}, Coord__X_out};  // Bit_Extender bit_extender_3
  assign bit_extender_4_out = {{1{Coord__Y_out[3]}}, Coord__Y_out};  // Bit_Extender bit_extender_4
  Adder #(.width(5)) adder_1 (.a(bit_extender_1_out), .b(bit_extender_2_out), .out(adder_1_out));  // open: cin, cout
  Adder #(.width(5)) adder_2 (.a(bit_extender_3_out), .b(bit_extender_4_out), .out(adder_2_out));  // open: cin, cout
  Comparator #(.width(5)) comparator_1 (
    .a(bit_extender_1_out), .b(bit_extender_3_out), .eq(comparator_1_eq));  // open: gt, lt
  Comparator #(.width(5)) comparator_2 (
    .a(bit_extender_2_out), .b(bit_extender_4_out), .eq(comparator_2_eq));  // open: gt, lt
  Comparator #(.width(5)) comparator_3 (
    .a(adder_1_out), .b(adder_2_out), .gt(comparator_3_gt), .eq(comparator_3_eq), .lt(comparator_3_lt));
  and and_1 (and_1_out, comparator_1_eq, comparator_2_eq);
  and and_2 (maior, comparator_3_gt, in_1);
  and and_3 (igual__soma, comparator_3_eq, in_1);
  and and_4 (menor, comparator_3_lt, in_1);
  and and_5 (igual__coordenadas, in_1, and_1_out);

  // Notes on the sheet:
  //   //ver problema com geração dos aleatórios 
  //   soma palpites
  //   soma Coord.
endmodule

module _8__visualizadorPalpites (
  input  [3:0] e3,
  output n,
  output [3:0] out_3
);

  wire and_2_out, and_3_out, and_4_out, and_5_out, and_6_out, and_7_out, and_8_out, not_1_out, not_2_out,
       not_3_out, not_4_out, not_5_out, not_6_out, not_7_out, not_8_out, not_9_out, not_10_out, not_11_out;

  not not_1 (not_1_out, e3[2]);
  not not_2 (not_2_out, e3[1]);
  not not_3 (not_3_out, e3[0]);
  not not_4 (not_4_out, e3[3]);
  not not_5 (not_5_out, e3[1]);
  not not_6 (not_6_out, e3[0]);
  not not_7 (not_7_out, e3[2]);
  not not_8 (not_8_out, e3[2]);
  not not_9 (not_9_out, e3[3]);
  not not_10 (not_10_out, e3[0]);
  not not_11 (not_11_out, e3[1]);
  and and_1 (out_3[3], e3[3], not_1_out, not_2_out, not_3_out);
  and and_2 (and_2_out, not_4_out, e3[2]);
  and and_3 (and_3_out, e3[2], not_5_out, not_6_out);
  and and_4 (and_4_out, e3[3], not_7_out, e3[0]);
  and and_5 (and_5_out, e3[3], not_8_out, e3[1]);
  and and_6 (and_6_out, not_9_out, e3[1]);
  and and_7 (and_7_out, e3[1], not_10_out);
  and and_8 (and_8_out, e3[3], not_11_out, e3[0]);
  or or_1 (out_3[2], and_2_out, and_3_out, and_4_out, and_5_out);
  or or_2 (out_3[1], and_6_out, and_7_out, and_8_out);

  assign n = e3[3];
  assign out_3[0] = e3[0];
endmodule

module \_9__cronômetro  (
  input  in_1,
  input  Pause,
  input  in_3,
  output acabou
);

  wire adder_1_out, and_1_out, and_2_out, and_3_out, and_4_out, and_5_out, and_6_out, and_7_out, and_8_out,
       and_9_out, and_10_out, and_12_out, and_13_out, clock_1_out;
  wire [3:0] bit_extender_1_out, bit_extender_2_out, bit_extender_3_out, bit_extender_4_out, d_ff_1_q,
       d_ff_5_q, d_ff_9_q, d_ff_13_q, subtractor_1_out, subtractor_2_out, subtractor_3_out, subtractor_4_out;

  Clock clock_1 (.out(clock_1_out));
  and and_1 (and_1_out, ~acabou, clock_1_out);  // AND_Gate
  and and_2 (and_2_out, and_1_out, Pause);
  assign bit_extender_1_out = {{3{1'b0}}, adder_1_out};  // Bit_Extender bit_extender_1
  Adder #(.width(1)) adder_1 (.a(1'b0), .b(in_3), .out(adder_1_out));  // open: cin, cout
  Subtractor #(.width(4)) subtractor_1 (.a(d_ff_1_q), .b(4'b0001), .out(subtractor_1_out));  // open: bin, bout
  D_Flip_Flop d_ff_1 (
    .clk(and_2_out), .D(subtractor_1_out[0]), .Q(d_ff_1_q[0]), .preset(and_3_out));  // open: Qn, en, reset
  D_Flip_Flop d_ff_2 (
    .clk(and_2_out), .D(subtractor_1_out[1]), .Q(d_ff_1_q[1]), .reset(and_3_out));  // open: Qn, preset, en
  D_Flip_Flop d_ff_3 (
    .clk(and_2_out), .D(subtractor_1_out[2]), .Q(d_ff_1_q[2]), .reset(and_3_out));  // open: Qn, preset, en
  D_Flip_Flop d_ff_4 (
    .clk(and_2_out), .D(subtractor_1_out[3]), .Q(d_ff_1_q[3]), .preset(and_3_out));  // open: Qn, en, reset
  and and_3 (and_3_out, d_ff_1_q[0], d_ff_1_q[1], d_ff_1_q[2], d_ff_1_q[3]);
  and and_4 (and_4_out, ~d_ff_1_q[3], ~d_ff_1_q[2], ~d_ff_1_q[1], ~d_ff_1_q[0]);  // AND_Gate
  assign bit_extender_2_out = {{3{1'b0}}, and_4_out};  // Bit_Extender bit_extender_2
  Subtractor #(.width(4)) subtractor_2 (
    .a(d_ff_5_q), .b(bit_extender_2_out), .out(subtractor_2_out));  // open: bin, bout
  D_Flip_Flop d_ff_5 (
    .clk(and_2_out), .D(subtractor_2_out[0]), .Q(d_ff_5_q[0]), .preset(and_6_out));  // open: Qn, en, reset
  D_Flip_Flop d_ff_6 (
    .clk(and_2_out), .D(subtractor_2_out[1]), .Q(d_ff_5_q[1]), .reset(and_6_out));  // open: Qn, preset, en
  D_Flip_Flop d_ff_7 (
    .clk(and_2_out), .D(subtractor_2_out[2]), .Q(d_ff_5_q[2]), .preset(and_6_out));  // open: Qn, en, reset
  D_Flip_Flop d_ff_8 (
    .clk(and_2_out), .D(subtractor_2_out[3]), .Q(d_ff_5_q[3]), .reset(and_6_out));  // open: Qn, preset, en
  and and_5 (and_5_out, ~d_ff_5_q[3], ~d_ff_5_q[2], ~d_ff_5_q[1], ~d_ff_5_q[0]);  // AND_Gate
  and and_6 (and_6_out, d_ff_5_q[0], d_ff_5_q[1], d_ff_5_q[2], d_ff_5_q[3]);
  Hex_Digit_Display hex_digit_display_1 (.value(d_ff_9_q));  // open: dp
  Hex_Digit_Display hex_digit_display_2 (.value(d_ff_13_q));  // open: dp
  and and_7 (and_7_out, and_4_out, and_5_out);
  LED led_1 (.in(in_1));
  LED led_2 (.in(in_1));
  Hex_Digit_Display hex_digit_display_3 (.value(d_ff_5_q));  // open: dp
  Hex_Digit_Display hex_digit_display_4 (.value(d_ff_1_q));  // open: dp
  assign bit_extender_3_out = {{3{1'b0}}, and_7_out};  // Bit_Extender bit_extender_3
  Subtractor #(.width(4)) subtractor_3 (
    .a(d_ff_9_q), .b(bit_extender_3_out), .out(subtractor_3_out));  // open: bin, bout
  D_Flip_Flop d_ff_9 (
    .clk(and_2_out), .D(subtractor_3_out[0]), .Q(d_ff_9_q[0]), .preset(and_8_out));  // open: Qn, en, reset
  D_Flip_Flop d_ff_10 (
    .clk(and_2_out), .D(subtractor_3_out[1]), .Q(d_ff_9_q[1]), .reset(and_8_out));  // open: Qn, preset, en
  D_Flip_Flop d_ff_11 (
    .clk(and_2_out), .D(subtractor_3_out[2]), .Q(d_ff_9_q[2]), .reset(and_8_out));  // open: Qn, preset, en
  D_Flip_Flop d_ff_12 (
    .clk(and_2_out), .D(subtractor_3_out[3]), .Q(d_ff_9_q[3]), .preset(and_8_out));  // open: Qn, en, reset
  and and_8 (and_8_out, d_ff_9_q[0], d_ff_9_q[1], d_ff_9_q[2], d_ff_9_q[3]);
  and and_9 (and_9_out, ~d_ff_9_q[3], ~d_ff_9_q[2], ~d_ff_9_q[1], ~d_ff_9_q[0]);  // AND_Gate
  assign bit_extender_4_out = {{3{1'b0}}, and_10_out};  // Bit_Extender bit_extender_4
  and and_10 (and_10_out, and_7_out, and_9_out);
  Subtractor #(.width(4)) subtractor_4 (
    .a(d_ff_13_q), .b(bit_extender_4_out), .out(subtractor_4_out));  // open: bin, bout
  D_Flip_Flop d_ff_13 (
    .clk(and_2_out), .D(subtractor_4_out[0]), .Q(d_ff_13_q[0]), .preset(and_13_out));  // open: Qn, en, reset
  D_Flip_Flop d_ff_14 (
    .clk(and_2_out), .D(subtractor_4_out[1]), .Q(d_ff_13_q[1]), .reset(and_13_out));  // open: Qn, preset, en
  D_Flip_Flop d_ff_15 (
    .clk(and_2_out), .D(subtractor_4_out[2]), .Q(d_ff_13_q[2]), .preset(and_13_out));  // open: Qn, en, reset
  D_Flip_Flop d_ff_16 (
    .clk(and_2_out), .D(subtractor_4_out[3]), .Q(d_ff_13_q[3]), .reset(and_13_out));  // open: Qn, preset, en
  and and_11 (acabou, and_10_out, and_12_out);
  and and_12 (and_12_out, ~d_ff_13_q[3], ~d_ff_13_q[2], ~d_ff_13_q[1], ~d_ff_13_q[0]);  // AND_Gate
  and and_13 (and_13_out, d_ff_13_q[0], d_ff_13_q[1], d_ff_13_q[2], d_ff_13_q[3]);

  // Other names for the same wires on the sheet: a = in_1
endmodule

module _10__parteDezena (
  input  [3:0] Constante_Recebida,
  input  Clock,
  input  Config,
  input  Setter,
  input  in_5,
  output [3:0] Display,
  output [3:0] Constante_Enviada
);

  wire and_1_out, and_2_out, and_3_out, and_4_out, and_5_out, bit_extender_1_out, or_1_out, or_2_out,
       or_3_out, or_4_out;
  wire [3:0] bit_extender_2_out, subtractor_1_out;

  Bit_Extender #(.in_width(4), .out_width(1)) bit_extender_1 (.in(Constante_Recebida), .out(bit_extender_1_out));
  and and_1 (and_1_out, bit_extender_1_out, ~Config);  // AND_Gate
  and and_2 (and_2_out, 1'b1, Config);
  and and_3 (and_3_out, Config, Setter);
  or or_1 (or_1_out, and_1_out, and_2_out);
  assign bit_extender_2_out = {{3{1'b0}}, or_1_out};  // Bit_Extender bit_extender_2
  or or_2 (or_2_out, Clock, and_3_out);
  Subtractor #(.width(4)) subtractor_1 (
    .a(Display), .b(bit_extender_2_out), .out(subtractor_1_out));  // open: bin, bout
  D_Flip_Flop d_ff_1 (
    .clk(or_2_out), .D(subtractor_1_out[0]), .Q(Display[0]), .preset(and_5_out), .reset(in_5));  // open: Qn, en
  D_Flip_Flop d_ff_2 (
    .clk(or_2_out), .D(subtractor_1_out[1]), .Q(Display[1]), .reset(or_3_out));  // open: Qn, preset, en
  D_Flip_Flop d_ff_3 (
    .clk(or_2_out), .D(subtractor_1_out[2]), .Q(Display[2]), .preset(and_5_out), .reset(in_5));  // open: Qn, en
  D_Flip_Flop d_ff_4 (
    .clk(or_2_out), .D(subtractor_1_out[3]), .Q(Display[3]), .reset(or_4_out));  // open: Qn, preset, en
  or or_3 (or_3_out, and_5_out, in_5);
  or or_4 (or_4_out, and_5_out, in_5);
  and and_4 (and_4_out, ~Display[3], ~Display[2], ~Display[1], ~Display[0]);  // AND_Gate
  and and_5 (and_5_out, Display[0], Display[1], Display[2], Display[3]);
  assign Constante_Enviada = {{3{1'b0}}, and_4_out};  // Bit_Extender bit_extender_3
endmodule

module _11__parteUnidade (
  input  [3:0] Constante_Recebida,
  input  Clock,
  input  Config,
  input  Setter,
  input  in_5,
  output [3:0] Display,
  output [3:0] Constante_Enviada
);

  wire and_1_out, and_2_out, and_3_out, and_4_out, and_5_out, bit_extender_1_out, or_1_out, or_2_out,
       or_3_out, or_4_out;
  wire [3:0] bit_extender_2_out, subtractor_1_out;

  Bit_Extender #(.in_width(4), .out_width(1)) bit_extender_1 (.in(Constante_Recebida), .out(bit_extender_1_out));
  and and_1 (and_1_out, bit_extender_1_out, ~Config);  // AND_Gate
  or or_1 (or_1_out, and_1_out, and_2_out);
  and and_2 (and_2_out, 1'b1, Config);
  and and_3 (and_3_out, Config, Setter);
  assign bit_extender_2_out = {{3{1'b0}}, or_1_out};  // Bit_Extender bit_extender_2
  or or_2 (or_2_out, Clock, and_3_out);
  Subtractor #(.width(4)) subtractor_1 (
    .a(Display), .b(bit_extender_2_out), .out(subtractor_1_out));  // open: bin, bout
  D_Flip_Flop d_ff_1 (
    .clk(or_2_out), .D(subtractor_1_out[0]), .Q(Display[0]), .preset(and_4_out), .reset(in_5));  // open: Qn, en
  D_Flip_Flop d_ff_2 (
    .clk(or_2_out), .D(subtractor_1_out[1]), .Q(Display[1]), .reset(or_3_out));  // open: Qn, preset, en
  or or_3 (or_3_out, and_4_out, in_5);
  D_Flip_Flop d_ff_3 (
    .clk(or_2_out), .D(subtractor_1_out[2]), .Q(Display[2]), .reset(or_4_out));  // open: Qn, preset, en
  or or_4 (or_4_out, and_4_out, in_5);
  D_Flip_Flop d_ff_4 (
    .clk(or_2_out), .D(subtractor_1_out[3]), .Q(Display[3]), .preset(and_4_out), .reset(in_5));  // open: Qn, en
  and and_4 (and_4_out, Display[0], Display[1], Display[2], Display[3]);
  and and_5 (and_5_out, ~Display[3], ~Display[2], ~Display[1], ~Display[0]);  // AND_Gate
  assign Constante_Enviada = {{3{1'b0}}, and_5_out};  // Bit_Extender bit_extender_3
endmodule

// [12]
module _12__relogioOrganizado (
  input  Clock,
  input  Config,
  input  dM,
  input  uM,
  input  dS,
  input  uS,
  input  Reset,
  output [3:0] out_8,
  output [3:0] out_9,
  output [3:0] out_10,
  output [3:0] out_11,
  output Fim
);

  wire and_1_out, bit_extender_1_out, bit_extender_2_out, bit_extender_3_out, bit_extender_4_out;
  wire [3:0] and_2_out, and_3_out, n10_partedezena_1_constante_enviada, n10_partedezena_2_constante_enviada,
       n11_parteunidade_1_constante_enviada, n11_parteunidade_2_constante_enviada;

  _10__parteDezena u_10_partedezena_1 (
    .Constante_Enviada(n10_partedezena_1_constante_enviada), .Display(out_8), .Constante_Recebida(and_2_out),
    .Clock(and_1_out), .Config(Config), .Setter(dM), .in_5(Reset));
  and and_1 (and_1_out, Clock, ~Config);  // AND_Gate
  assign and_2_out = and_3_out & n11_parteunidade_1_constante_enviada;  // AND_Gate and_2, 4 bits wide
  _11__parteUnidade u_11_parteunidade_1 (
    .Constante_Recebida(and_3_out), .Constante_Enviada(n11_parteunidade_1_constante_enviada),
    .Display(out_9), .Clock(and_1_out), .Setter(uM), .Config(Config), .in_5(Reset));
  assign and_3_out = n11_parteunidade_2_constante_enviada & n10_partedezena_2_constante_enviada;  // AND_Gate and_3, 4 bits wide
  _10__parteDezena u_10_partedezena_2 (
    .Constante_Enviada(n10_partedezena_2_constante_enviada), .Display(out_10),
    .Constante_Recebida(n11_parteunidade_2_constante_enviada), .Clock(and_1_out), .Config(Config),
    .Setter(dS), .in_5(Reset));
  _11__parteUnidade u_11_parteunidade_2 (
    .Constante_Recebida(4'b0001), .Constante_Enviada(n11_parteunidade_2_constante_enviada), .Display(out_11),
    .Clock(and_1_out), .Setter(uS), .Config(Config), .in_5(Reset));
  Bit_Extender #(.in_width(4), .out_width(1)) bit_extender_1 (
    .in(n10_partedezena_1_constante_enviada), .out(bit_extender_1_out));
  Bit_Extender #(.in_width(4), .out_width(1)) bit_extender_2 (.in(and_2_out), .out(bit_extender_2_out));
  Bit_Extender #(.in_width(4), .out_width(1)) bit_extender_3 (
    .in(n10_partedezena_2_constante_enviada), .out(bit_extender_3_out));
  Bit_Extender #(.in_width(4), .out_width(1)) bit_extender_4 (
    .in(n11_parteunidade_2_constante_enviada), .out(bit_extender_4_out));
  and and_4 (Fim, bit_extender_1_out, bit_extender_2_out, bit_extender_3_out, bit_extender_4_out);
endmodule

module _13__circuitoCore (
  input  in_1,
  input  in_2,
  input  in_3,
  input  in_4,
  input  in_5,
  input  Palpite_do,
  input  in_7,
  input  in_8,
  input  Turnout,
  input  Reset,
  output Chutando_X,
  output Chutando_Y,
  output Resultado,
  output Maior,
  output Igual,
  output Menor,
  output Acertou
);

  wire _5_clockx, _5_clockx_2, _8_2_n, _8_n, and_1_out, and_2_out, and_3_out, button_1_out, button_2_out;
  wire [3:0] _1_2_out_3, _1_out_3, _6_2_out_4, _6_out_4, _8_2_out_3, _8_out_3, multiplexer_1_out;

  Button button_1 (.out(button_1_out));
  Button button_2 (.out(button_2_out));
  Multiplexer #(.width(4)) multiplexer_1 (
    .in0({in_1, in_2, in_3, in_4}), .in1({in_5, Palpite_do, in_7, in_8}), .out(multiplexer_1_out),
    .sel(Turnout));  // open: en
  _5__LEDS _5 (
    .Chutar(button_1_out), .in_2(button_2_out), .x(Chutando_X), .y(Chutando_Y), .c(Resultado),
    .clockX(_5_clockx), .clockX_2(_5_clockx_2));
  _6__memoriaPalpite _6 (.in_1(_5_clockx), .in_2(multiplexer_1_out), .reset(Reset), .out_4(_6_out_4));
  _8__visualizadorPalpites _8 (.e3(_6_out_4), .n(_8_n), .out_3(_8_out_3));
  _6__memoriaPalpite _6_2 (.in_1(_5_clockx_2), .in_2(multiplexer_1_out), .reset(Reset), .out_4(_6_2_out_4));
  _8__visualizadorPalpites _8_2 (.e3(_6_2_out_4), .n(_8_2_n), .out_3(_8_2_out_3));
  _7_Segment_Display u_7_segment_display_1 (.g(_8_n));  // open: f, a, b, e, d, c, dp
  Hex_Digit_Display hex_digit_display_1 (.value(_8_out_3));  // open: dp
  _7_Segment_Display u_7_segment_display_2 (.g(_8_2_n));  // open: f, a, b, e, d, c, dp
  Hex_Digit_Display hex_digit_display_2 (.value(_8_2_out_3));  // open: dp
  _7__somador _7 (
    .palpite_Coord__x(_6_out_4), .palpite_Coord__Y(_6_2_out_4), .in_1(Resultado), .in_4(and_1_out),
    .maior(Maior), .igual__soma(Igual), .menor(Menor), .igual__coordenadas(Acertou));
  and and_1 (and_1_out, Chutando_X, Acertou);
  and and_2 (and_2_out, Acertou, ~Turnout);  // AND_Gate
  and and_3 (and_3_out, Acertou, Turnout);
  Hex_Digit_Display hex_digit_display_3 (.value(_1_out_3));  // open: dp
  _1__Pontuador _1 (.in_1(and_2_out), .out_3(_1_out_3));  // open: Reset
  Hex_Digit_Display hex_digit_display_4 (.value(_1_2_out_3));  // open: dp
  _1__Pontuador _1_2 (.in_1(and_3_out), .out_3(_1_2_out_3));  // open: Reset

  // Other names for the same wires on the sheet: C = Chutando_X

  // Notes on the sheet:
  //   Palpite do
  //   jogador 0
  //   jogador 1
  //   Mudar estado
  //   Coord. X
  //   Coord. Y
  //   Pontuação do 
  //   jogador 0
  //   Pontuação do 
  //   jogador 1
endmodule

module _15__placarFinal (
  input  [3:0] placar0,
  input  [3:0] placar1,
  input  tempo0,
  input  tempo1,
  output venceu0,
  output empate,
  output venceu1,
  output FimdeJogo
);

  wire and_1_out, and_2_out, and_4_out, comparator_1_eq, comparator_2_eq, comparator_3_eq, comparator_3_gt,
       comparator_3_lt;

  Comparator #(.width(4)) comparator_1 (.a(placar0), .b(4'b1111), .eq(comparator_1_eq));  // open: gt, lt
  Comparator #(.width(4)) comparator_2 (.a(placar1), .b(4'b1111), .eq(comparator_2_eq));  // open: gt, lt
  Comparator #(.width(4)) comparator_3 (
    .a(placar0), .b(placar1), .gt(comparator_3_gt), .eq(comparator_3_eq), .lt(comparator_3_lt));
  and and_1 (and_1_out, tempo0, tempo1);
  or or_1 (FimdeJogo, and_1_out, comparator_2_eq, comparator_1_eq);
  and and_2 (and_2_out, comparator_3_gt, and_1_out);
  and and_3 (empate, comparator_3_eq, and_1_out);
  and and_4 (and_4_out, comparator_3_lt, and_1_out);
  or or_2 (venceu0, comparator_1_eq, and_2_out);
  or or_3 (venceu1, comparator_2_eq, and_4_out);
endmodule

module _16__mostraEmDecimal (
  input  e3,
  input  e2,
  input  e1,
  input  e0,
  output [3:0] d,
  output [3:0] u
);

  wire and_1_out, and_2_out, and_4_out, and_5_out, and_6_out, and_7_out, not_1_out, not_2_out, not_3_out,
       not_4_out, not_5_out, or_1_out;

  and and_1 (and_1_out, e3, e1);
  and and_2 (and_2_out, e3, e2);
  not not_1 (not_1_out, e2);
  and and_3 (u[3], e3, not_1_out, not_2_out);
  not not_2 (not_2_out, e1);
  not not_3 (not_3_out, e3);
  and and_4 (and_4_out, not_3_out, e2);
  and and_5 (and_5_out, e2, e1);
  not not_4 (not_4_out, e3);
  and and_6 (and_6_out, not_4_out, e1);
  and and_7 (and_7_out, e3, e2, not_5_out);
  not not_5 (not_5_out, e1);
  assign d = {{3{1'b0}}, or_1_out};  // Bit_Extender bit_extender_1
  or or_1 (or_1_out, and_1_out, and_2_out);
  or or_2 (u[2], and_4_out, and_5_out);
  or or_3 (u[1], and_6_out, and_7_out);

  assign u[0] = e0;
endmodule

module _17__mudaJogador (
  input  Resultado,
  input  Z1,
  input  Z0,
  output out_4
);

  wire and_1_out, multiplexer_1_out, not_1_out;

  and and_1 (and_1_out, Resultado, ~multiplexer_1_out);  // AND_Gate
  Multiplexer #(.enable("false")) multiplexer_1 (.in0(Z1), .in1(Z0), .out(multiplexer_1_out), .sel(out_4));
  D_Flip_Flop d_ff_1 (.clk(and_1_out), .D(not_1_out), .Q(out_4));  // open: Qn, preset, en, reset
  not not_1 (not_1_out, out_4);
endmodule

module _18__logicaEstadoPermanente (
  input  in_1,
  input  Reset,
  output out_3
);

  wire clock_1_out, d_ff_1_q;

  Clock clock_1 (.out(clock_1_out));
  logicaStart logicastart_1 (.s1(in_1), .x(d_ff_1_q), .e1(out_3));
  D_Flip_Flop d_ff_1 (.clk(clock_1_out), .D(out_3), .Q(d_ff_1_q), .reset(Reset));  // open: Qn, preset, en
endmodule

module startt (
  input  Start,
  input  Clock,
  output out_3
);

  wire d_ff_1_q;

  D_Flip_Flop d_ff_1 (.clk(Clock), .D(out_3), .Q(d_ff_1_q));  // open: Qn, preset, en, reset
  estadosStart estadosstart_1 (.e1(Start), .x(d_ff_1_q), .s0(out_3));
endmodule

module estadosStart (
  input  e1,
  input  x,
  output s0
);

  or or_1 (s0, x, e1);
endmodule

module logicaStart (
  input  s1,
  input  x,
  output e1
);

  or or_1 (e1, x, s1);
endmodule
